# Fritzing sketch Projeto_1_SD (saved by Fritzing 0.9.3b)
breadboards: 1

parts:
  Componente1 = Arduino Uno (Rev3)
  R1 = Photocell (LDR) [package=THT]
  R2 = Temperature Sensor (Thermistor) [thermistor_type=NTC package=THT]
  R3 = Resistor [tolerance=±5% resistance=4.7k package="2512 [SMD]"]
  R4 = Resistor [tolerance=±5% resistance=10k package="2512 [SMD]"]
  LED1 = LED - 3mm [color="Green (555nm)" package="3 mm [THT]"]

nets:
  N1: Componente1.A0, R1.pin_1, R4.Pin_0
  N2: Componente1.A1, R2.pin_1, R3.Pin_0
  N3: Componente1.D13/SCK, LED1.anode
  N4: Componente1.GND, R3.Pin_1, R4.Pin_1, LED1.cathode
  N5: Componente1.5V, R1.pin_0, R2.pin_0
